# Fritzing sketch full-module (saved by Fritzing 0.9.9b)
breadboards: 2

parts:
  J2 = Basic Servo
  M2 = DOIT Esp32 DevKit v1 (30 pins long, 11 pins width) [part_number=ESP32S-PIN30]
  Part4 = RFID-RC522-v3
  HC-SR04_Sensor_3 = HC-SR04 Ultrasonic Distance Sensor
  LED2 = LED - 3mm [color="Green (570nm)" current=0.030 package="3 mm [THT]"]
  LED3 = LED - 3mm [color="Red (633nm)" current=0.030 package="3 mm [THT]"]
  R1 = Resistor [tolerance=±5% resistance=1k package="1206 [SMD]"]
  R2 = Resistor [tolerance=±5% resistance=1k package="1206 [SMD]"]
  USBTTL1 = Micro USB B Plug  # not connected

nets:
  GND: J2.gnd, M2.GND, Part4.GND, HC-SR04_Sensor_3.GND, LED2.cathode, LED3.cathode
  VCC: J2.vcc, M2.VIN, HC-SR04_Sensor_3.VCC
  N1: J2.pulse, M2.D12
  3V3: M2.3V3, Part4.3.3V
  N2: M2.D2, HC-SR04_Sensor_3.TRIG
  N3: M2.D4, HC-SR04_Sensor_3.ECHO
  N4: M2.D18, Part4.SCK
  N5: M2.D19, Part4.MISO
  N6: M2.D21, Part4.SDA
  N7: M2.D22, Part4.RST
  N8: M2.D23, Part4.MOSI
  N9: M2.D25, R2.Pin_1
  N10: M2.D26, R1.Pin_1
  N11: LED2.anode, R1.Pin_0
  N12: LED3.anode, R2.Pin_0

custom parts:
  DOIT Esp32 DevKit v1 (30 pins long, 11 pins width): The DOIT Esp32 DevKit v1 is one of the development board created by DOIT to evaluate the ESP-WROOM-32 module. It is based on the ESP32 microcontroller that boasts Wifi, Bluetooth, Ethernet and Low Power support all in a single chip. (vanepp) made breadboard work, adjusted pin numbering and labels and reduced size of schematic and cleaned up pcb. This chip is 30pins long (2 x15) and 11 pins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
  RFID-RC522-v3: A simple China made RFID-RC522 Reader (6x4 cm); do check the pin labels, as this is a MFRC522 based clone.
